# Fritzing sketch Raddar_buzzer (saved by Fritzing 0.9.3b)
breadboards: 1

parts:
  Composant1 = Arduino Nano (Rev3.0)
  LED1 = LED - 5mm [color="Red (633nm)" package="5 mm [THT]"]
  LED2 = LED - 5mm [color="Orange (605nm)" package="5 mm [THT]"]
  LED3 = LED - 5mm [color="Green (565nm)" package="5 mm [THT]"]
  R1 = Resistor [tolerance=±5% resistance=100 package=THT]
  hc-sr1 = hc-sr04
  J1 = Piezo Speaker

nets:
  GND: Composant1.GND, R1.Pin_0, hc-sr1.GND, J1.pin1
  N1: Composant1.D3, J1.pin2
  N2: Composant1.D6, hc-sr1.Trig
  N3: Composant1.D7, hc-sr1.Echo
  N4: Composant1.D11/MOSI, LED1.anode
  N5: Composant1.D12/MISO, LED2.anode
  5V: Composant1.5V, hc-sr1.VCC
  N6: Composant1.D13/SCK, LED3.anode
  N7: LED1.cathode, LED2.cathode, LED3.cathode, R1.Pin_1
